# Fritzing sketch Performance_tests_Nucleo_L476RG (saved by Fritzing 1.0.2b)
breadboards: 1

parts:
  J1 = STM32 Nucleo boards
  SEN1 = US-100 Ultrasonic Distance Sensor
  Componente3 = Power Profiler Kit II [chip_label="Power Profiler Kit II" package=QFN]

nets:
  N1: J1.E5V, Componente3.VOUT
  N2: J1.D2, SEN1.TRIG
  N3: J1.D3_PWM, SEN1.ECHO
  3V3: J1.3V3, SEN1.VCC
  GND: J1.GND, SEN1.GND, SEN1.GND-2, Componente3.GND

notes:
  *PPK2 works as power supply unit:
  - It is feed by USB/Data Power cable.
  - Its connected in mode SMU (Source Meter Unit) .
  VOUT <-> Nucleo E5V Pin
  GND <-> GND
  Pin 6
  E5V
  ** All GND pins in all boards and components should be connected toghether!
  Attention!
  The nucleo board is feed by E5V pin (5V)!
  Do the following procedure to activate it:
  1. Connect the jumper between pin 2 and pin 3 of JP5 (E5V)
  2. Check that JP1 is removed
  3. Connect the external power source to E5V (5V)
  4. Power on the external power supply to 5V for E5V
  5. Check that LD3 is turned ON
  6. Connect the PC to USB connector CN1
  You can use St-Link for programming and debugging.
  Nucleo L475RG Power Consumption Tests

custom parts:
  Power Profiler Kit II: Nordic Power Profiler Kit II
